# Fritzing sketch pcb1 (saved by Fritzing 0.9.3b)
breadboards: 1

parts:
  Arduino = Arduino Uno (Rev3)
  HC-06_Header = Hirose DF13 Series Header [part_number=DF13A-4P-1.25H package=DF13A-4P-1.25H]
  HC-SR04_Header = Hirose DF13 Series Header [part_number=DF13A-4P-1.25H package=DF13A-4P-1.25H]
  9v = Header 8 [package=bm08b-srss-tb]
  5v = Header 8 [package=bm08b-srss-tb]
  3_3v = Header 8 [package=bm08b-srss-tb]
  GND = Header 8 [package=bm08b-srss-tb]
  R1 = Trimmer Potentiometer [maximum_resistance=10kΩ package=THT]
  R2 = Temperature Sensor (Thermistor) [thermistor_type=NTC package=THT]

nets:
  N1: Arduino.A0, R1.leg2, R2.pin_0
  N2: Arduino.GND, HC-06_Header.2, HC-SR04_Header.1, GND.1, GND.2, GND.3, GND.4, GND.5, GND.6, GND.7, GND.8, R1.wiper
  N3: Arduino.D0/RX, HC-06_Header.3
  N4: Arduino.D1/TX, HC-06_Header.4
  N5: Arduino.D2, HC-SR04_Header.2
  N6: Arduino.D3_PWM, HC-SR04_Header.3
  N7: Arduino.3V3, 3_3v.1, 3_3v.2, 3_3v.3, 3_3v.4, 3_3v.5, 3_3v.6, 3_3v.7, 3_3v.8, R2.pin_1
  N8: Arduino.5V, HC-06_Header.1, HC-SR04_Header.4, 5v.1, 5v.2, 5v.3, 5v.4, 5v.5, 5v.6, 5v.7, 5v.8
  N9: Arduino.VIN, 9v.1, 9v.2, 9v.3, 9v.4, 9v.5, 9v.6, 9v.7, 9v.8
