# Fritzing sketch pcb2 (saved by Fritzing 0.9.3b)

parts:
  U1 = Hirose DF13 Series Header [part_number=DF13A-8P-1.25H package=DF13A-8P-1.25H]
  U2 = Hirose DF13 Series Header [part_number=DF13A-8P-1.25H package=DF13A-8P-1.25H]
  Arduino1 = Arduino Uno (Rev3)
  part = Header 2 [part_number="Motor 1" package=jst-2-pth-kit]
  part_2 = Header 2 [part_number="Motor 2" package=jst-2-pth-kit]
  U6 = TLP621 [package=THT]
  U7 = TLP621 [package=THT]
  U8 = TLP621 [package=THT]
  U9 = TLP621 [package=THT]
  R9 = Resistor [tolerance=±5% resistance=47k package=THT]
  R10 = Resistor [tolerance=±5% resistance=220 package=THT]
  R11 = Resistor [tolerance=±5% resistance=220 package=THT]
  R12 = Resistor [tolerance=±5% resistance=47k package=THT]
  R13 = Resistor [tolerance=±5% resistance=220 package=THT]
  R14 = Resistor [tolerance=±5% resistance=47k package=THT]
  R15 = Resistor [tolerance=±5% resistance=47k package=THT]
  R16 = Resistor [tolerance=±5% resistance=220 package=THT]
  part_3 = Header 2 [part_number=Bremslicht package=jst-2-pth-kit]
  part_4 = Header 2 [part_number="Linker Blinker" package=jst-2-pth-kit]
  part_5 = Header 2 [part_number="Rechter Blinker" package=jst-2-pth-kit]

nets:
  N1: U1.1, Arduino1.D10_PWM/SS
  N2: U1.2, Arduino1.D8
  N3: U1.3, part.1
  N4: U1.4, U1.5, U2.4, U2.5, Arduino1.GND, U6.Pin_2, U6.Pin_3, U7.Pin_2, U7.Pin_3, U8.Pin_2, U8.Pin_3, U9.Pin_2, U9.Pin_3, part_3.1, part_4.1, part_5.1
  N5: U1.6, part.2
  N6: U1.7, Arduino1.D11_PWM/MOSI
  N7: U1.8, Arduino1.VIN
  N8: U2.1, Arduino1.5V, R9.Pin_0, R10.Pin_0, R11.Pin_0, R12.Pin_0, R13.Pin_0, R14.Pin_0, R15.Pin_0, R16.Pin_0
  N9: U2.2, Arduino1.D6_PWM
  N10: U2.3, part_2.1
  N11: U2.6, part_2.2
  N12: U2.7, Arduino1.D5_PWM
  N13: U2.8, Arduino1.D9_PWM
  N14: Arduino1.A2, U9.Pin_4, R15.Pin_1
  N15: Arduino1.A3, U8.Pin_4, R14.Pin_1
  N16: Arduino1.A4/SDA, U7.Pin_4, R12.Pin_1
  N17: Arduino1.D12/MISO, part_5.2
  N18: Arduino1.A5/SCL, U6.Pin_4, R9.Pin_1
  N19: Arduino1.D4, part_3.2
  N20: Arduino1.D7, part_4.2
  N21: U6.Pin_1, R10.Pin_1
  N22: U7.Pin_1, R11.Pin_1
  N23: U8.Pin_1, R13.Pin_1
  N24: U9.Pin_1, R16.Pin_1
